// Logisim project exerciceb4.circ as structural Verilog: 5 circuits, main circuit main
module main (
  output SA,
  output SB,
  output [3:0] us,
  output [3:0] um,
  output [2:0] ds,
  output [2:0] dm
);

  wire clk_out;
  wire [6:0] aff_7seg_1_out_7seg;

  Clock clk (.out(clk_out));
  Clock sysclk ();  // open: out
  montre montre_1 (.clock(clk_out), .S(SA), .s1(us), .s2(ds));
  aff_7seg aff_7seg_1 (.in_bin(us), .out_7seg(aff_7seg_1_out_7seg));
  _7_Segment_Display u_7_segment_display_1 (
    .g(aff_7seg_1_out_7seg[6]), .f(aff_7seg_1_out_7seg[5]), .a(aff_7seg_1_out_7seg[0]),
    .b(aff_7seg_1_out_7seg[1]), .e(aff_7seg_1_out_7seg[4]), .d(aff_7seg_1_out_7seg[3]),
    .c(aff_7seg_1_out_7seg[2]));  // open: dp
  montre montre_2 (.clock(SA), .S(SB), .s1(um), .s2(dm));
endmodule

module montre (
  input  clock,
  output S,
  output [3:0] s1,
  output [2:0] s2
);

  wire comparator_1_eq, comparator_2_eq, d_ff_1_q;

  Counter #(.width(4), .max('hf)) counter_1 (
    .load(comparator_1_eq), .up(1'b1), .count(1'b1), .clk(clock), .D(4'b0000), .Q(s1));  // open: clr, carry
  Comparator #(.width(4), .mode("unsigned")) comparator_1 (.a(s1), .b(4'b1001), .eq(comparator_1_eq));  // open: gt, lt
  D_Flip_Flop d_ff_1 (.D(comparator_1_eq), .clk(clock), .Q(d_ff_1_q));  // open: Qn, preset, reset
  Counter #(.width(3), .max('h7)) counter_2 (
    .load(comparator_2_eq), .up(1'b1), .count(1'b1), .clk(d_ff_1_q), .D(3'b000), .Q(s2));  // open: clr, carry
  Comparator #(.width(3), .mode("unsigned")) comparator_2 (.a(s2), .b(3'b101), .eq(comparator_2_eq));  // open: gt, lt
  D_Flip_Flop d_ff_2 (.D(comparator_2_eq), .clk(d_ff_1_q), .Q(S));  // open: Qn, preset, reset
endmodule

module basic (
  input  clock1,
  output K,
  output E,
  output J,
  output F,
  output G,
  output H,
  output I,
  output A,
  output B,
  output C,
  output D
);

  wire comparator_1_eq, m1_s;
  wire [2:0] m1_s2, m2_s2;
  wire [3:0] bitselector_1_out, bitselector_2_out, m1_s1, m2_s1, multiplexer_1_out;
  wire [26:0] C1_q;

  Counter #(.width(27), .max('h7ffffff)) C1 (
    .up(1'b1), .count(1'b1), .clk(clock1), .D({27{1'b0}}), .Q(C1_q));  // open: clr, load, carry
  Comparator #(.width(27)) comparator_1 (.a(27'h4), .b(C1_q), .eq(comparator_1_eq));  // open: gt, lt
  Multiplexer #(.select(2), .width(4), .enable("false")) multiplexer_1 (
    .in0(m1_s1), .in1(bitselector_1_out), .in2(m2_s1), .in3(bitselector_2_out), .out(multiplexer_1_out),
    .sel(C1_q[1:0]));
  Decoder #(.select(2)) decoder_1 (.out0(A), .out1(B), .out2(C), .out3(D), .sel(C1_q[1:0]), .en(1'b1));
  aff_7seg seg (.in_bin(multiplexer_1_out), .out_7seg({K, J, I, H, G, F, E}));
  montre m1 (.clock(comparator_1_eq), .S(m1_s), .s1(m1_s1), .s2(m1_s2));
  BitSelector #(.width(3), .group(4)) bitselector_1 (.in(m1_s2), .out(bitselector_1_out), .sel(1'b0));
  montre m2 (.clock(m1_s), .s1(m2_s1), .s2(m2_s2));  // open: S
  BitSelector #(.width(3), .group(4)) bitselector_2 (.in(m2_s2), .out(bitselector_2_out), .sel(1'b0));
endmodule

module aff_7seg (
  input  [3:0] in_bin,
  output [6:0] out_7seg
);

  wire nand_1_out, nand_2_out, nand_3_out, nand_4_out, nand_5_out, nand_6_out, nand_7_out, nand_8_out,
       nand_9_out;

  nand nand_1 (nand_1_out, ~in_bin[2], ~in_bin[0]);  // NAND_Gate
  nand nand_2 (nand_2_out, in_bin[2], in_bin[0]);
  nand nand_3 (nand_3_out, in_bin[1], in_bin[0]);
  nand nand_4 (nand_4_out, ~in_bin[1], ~in_bin[0]);  // NAND_Gate
  nand nand_5 (nand_5_out, in_bin[2], ~in_bin[1], in_bin[0]);  // NAND_Gate
  nand nand_6 (nand_6_out, ~in_bin[2], in_bin[1]);  // NAND_Gate
  nand nand_7 (nand_7_out, in_bin[1], ~in_bin[0]);  // NAND_Gate
  nand nand_8 (nand_8_out, in_bin[2], ~in_bin[1]);  // NAND_Gate
  nand nand_9 (nand_9_out, in_bin[2], ~in_bin[0]);  // NAND_Gate
  nand nand_10 (out_7seg[0], ~in_bin[3], nand_1_out, nand_2_out, nand_3_out);  // NAND_Gate
  nand nand_11 (out_7seg[1], nand_3_out, nand_4_out, in_bin[2]);
  nand nand_12 (out_7seg[2], ~in_bin[2], ~in_bin[0], in_bin[1]);  // NAND_Gate
  nand nand_13 (out_7seg[3], nand_1_out, nand_5_out, nand_6_out, nand_7_out);
  nand nand_14 (out_7seg[4], nand_7_out, nand_1_out);
  nand nand_15 (out_7seg[5], ~in_bin[3], nand_4_out, nand_8_out, nand_9_out);  // NAND_Gate
  nand nand_16 (out_7seg[6], ~in_bin[3], nand_9_out, nand_6_out, nand_8_out);  // NAND_Gate

  // Other names for the same wires on the sheet: A = in_bin[0]; B = in_bin[1]; C = in_bin[2]; D = in_bin[3]
endmodule

// decodeur_7_segments
module test_7seg_decodeur (
  input  [3:0] in_1
);

  wire [6:0] aff_7seg_1_out_7seg;

  aff_7seg aff_7seg_1 (.in_bin(in_1), .out_7seg(aff_7seg_1_out_7seg));
  LED a (.in(aff_7seg_1_out_7seg[0]));
  LED b (.in(aff_7seg_1_out_7seg[1]));
  LED f (.in(aff_7seg_1_out_7seg[5]));
  LED g (.in(aff_7seg_1_out_7seg[6]));
  LED e (.in(aff_7seg_1_out_7seg[4]));
  LED c (.in(aff_7seg_1_out_7seg[2]));
  LED d (.in(aff_7seg_1_out_7seg[3]));
endmodule
